# Fritzing sketch LEDBarGraph_Nano (saved by Fritzing 0.9.2b)
breadboards: 1

parts:
  Part1 = Arduino Nano (Rev3.0)
  R7 = Resistor [tolerance=±5% resistance=470 package=THT]
  R5 = Resistor [tolerance=±5% resistance=470 package=THT]
  R6 = Resistor [tolerance=±5% resistance=470 package=THT]
  R4 = Resistor [tolerance=±5% resistance=470 package=THT]
  R3 = Resistor [tolerance=±5% resistance=470 package=THT]
  R1 = Resistor [tolerance=±5% resistance=470 package=THT]
  R2 = Resistor [tolerance=±5% resistance=470 package=THT]
  U2 = 7-SEGMENT-DISPLAY-1_-RED [package=7-segment-1_pth]
  U1 = 7-SEGMENT-DISPLAY-1_-RED [package=7-segment-1_pth]

nets:
  N1: Part1.D2, R7.Pin_0
  N2: Part1.D3, R6.Pin_0
  N3: Part1.D4, R5.Pin_0
  N4: Part1.D5, R4.Pin_0
  N5: Part1.D6, R3.Pin_0
  N6: Part1.D7, R2.Pin_0
  N7: Part1.D8, R1.Pin_0
  N8: R7.Pin_1, U2.G
  N9: R5.Pin_1, U2.G2
  N10: R4.Pin_1, U1.G
  N11: R3.Pin_1, U1.F
  N12: R1.Pin_1, U1.A
  N13: R2.Pin_1, U1.G2
